// Logisim project CompBasedArch.circ as structural Verilog: 4 circuits, main circuit main
module main (
);

  wire clock_1_out;
  wire [3:0] registers_1_out_18, registers_1_out_18_2, registers_1_out_19, registers_1_out_19_2;
  wire [7:0] counters_1_out_11, counters_1_out_12, counters_1_out_13, registers_1_out_16, registers_1_out_17,
       rom_1_data_2;
  wire [30:0] rom_1_data;

  counters counters_1 (
    .in_1(counters_1_out_11), .in_2(clock_1_out), .in_3(rom_1_data[18]), .in_4(rom_1_data[17]),
    .in_5(rom_1_data[16]), .in_6(rom_1_data[15]), .in_7(rom_1_data[14]), .in_8(rom_1_data[13]),
    .in_9(rom_1_data[12]), .in_10(rom_1_data[11]), .out_11(counters_1_out_11), .out_12(counters_1_out_12),
    .out_13(counters_1_out_13));
  registers registers_1 (
    .in_3(rom_1_data[30]), .in_4(rom_1_data[29]), .in_5(rom_1_data[28]), .in_6(rom_1_data[27]),
    .in_7(rom_1_data[26]), .in_8(rom_1_data[25]), .in_9(rom_1_data[24]), .in_10(rom_1_data[23]),
    .in_11(rom_1_data[22]), .in_12(rom_1_data[21]), .in_13(rom_1_data[20]), .in_14(rom_1_data[19]),
    .in_2(clock_1_out), .in_1(counters_1_out_11), .out_15(counters_1_out_11), .out_16(registers_1_out_16),
    .out_17(registers_1_out_17), .out_18({registers_1_out_18_2, registers_1_out_18}),
    .out_19({registers_1_out_19_2, registers_1_out_19}));
  assign counters_1_out_11 = rom_1_data[2] ? rom_1_data_2 : 8'bz;  // Controlled_Buffer controlled_buffer_1
  Clock clock_1 (.out(clock_1_out));
  Hex_Digit_Display hex_digit_display_1 (.value(counters_1_out_11[7:4]));  // open: dp
  Hex_Digit_Display hex_digit_display_2 (.value(counters_1_out_11[3:0]));  // open: dp
  Hex_Digit_Display hex_digit_display_3 (.value(registers_1_out_16[7:4]));  // open: dp
  Hex_Digit_Display hex_digit_display_4 (.value(registers_1_out_16[3:0]));  // open: dp
  Hex_Digit_Display hex_digit_display_5 (.value(counters_1_out_12[7:4]));  // open: dp
  Hex_Digit_Display hex_digit_display_6 (.value(counters_1_out_12[3:0]));  // open: dp
  Hex_Digit_Display hex_digit_display_7 (.value(registers_1_out_17[7:4]));  // open: dp
  Hex_Digit_Display hex_digit_display_8 (.value(registers_1_out_17[3:0]));  // open: dp
  Hex_Digit_Display hex_digit_display_9 (.value(counters_1_out_13[7:4]));  // open: dp
  Hex_Digit_Display hex_digit_display_10 (.value(counters_1_out_13[3:0]));  // open: dp
  ROM #(.dataWidth(31)) rom_1 (.addr(counters_1_out_13), .data({rom_1_data[30:11], rom_1_data_2, rom_1_data[2:0]}));
  alu alu_1 (
    .in_3(rom_1_data[1]), .in_4(rom_1_data[0]), .in_1(registers_1_out_16), .in_2(registers_1_out_17),
    .out_5(counters_1_out_11));
  Hex_Digit_Display hex_digit_display_11 (.value(registers_1_out_18_2));  // open: dp
  Hex_Digit_Display hex_digit_display_12 (.value(registers_1_out_18));  // open: dp
  Hex_Digit_Display hex_digit_display_13 (.value(registers_1_out_19_2));  // open: dp
  Hex_Digit_Display hex_digit_display_14 (.value(registers_1_out_19));  // open: dp

  // Notes on the sheet:
  //   contents of rom_1 (hex, n*v repeats v):
  //   800 4804
endmodule

module registers (
  input  [7:0] in_1,
  input  in_2,
  input  in_3,
  input  in_4,
  input  in_5,
  input  in_6,
  input  in_7,
  input  in_8,
  input  in_9,
  input  in_10,
  input  in_11,
  input  in_12,
  input  in_13,
  input  in_14,
  output [7:0] out_15,
  output [7:0] out_16,
  output [7:0] out_17,
  output [7:0] out_18,
  output [7:0] out_19
);

  Register register_1 (.D(in_1), .en(in_3), .Q(out_16), .clk(in_2), .clr(in_5));
  assign out_15 = in_4 ? out_16 : 8'bz;  // Controlled_Buffer controlled_buffer_1
  Register register_2 (.D(in_1), .en(in_6), .Q(out_17), .clk(in_2), .clr(in_8));
  assign out_15 = in_7 ? out_17 : 8'bz;  // Controlled_Buffer controlled_buffer_2
  Register register_3 (.D(in_1), .en(in_9), .Q(out_18), .clk(in_2), .clr(in_11));
  assign out_15 = in_10 ? out_18 : 8'bz;  // Controlled_Buffer controlled_buffer_3
  assign out_15 = in_13 ? out_19 : 8'bz;  // Controlled_Buffer controlled_buffer_4
  Register register_4 (.D(in_1), .en(in_12), .Q(out_19), .clk(in_2), .clr(in_14));
endmodule

module counters (
  input  [7:0] in_1,
  input  in_2,
  input  in_3,
  input  in_4,
  input  in_5,
  input  in_6,
  input  in_7,
  input  in_8,
  input  in_9,
  input  in_10,
  output [7:0] out_11,
  output [7:0] out_12,
  output [7:0] out_13
);

  Counter counter_1 (.load(in_3), .D(in_1), .count(in_6), .Q(out_12), .clk(in_2), .clr(in_5));  // open: carry, up
  assign out_11 = in_4 ? out_12 : 8'bz;  // Controlled_Buffer controlled_buffer_1
  Counter counter_2 (.load(in_7), .D(in_1), .count(in_10), .Q(out_13), .clk(in_2), .clr(in_9));  // open: carry, up
  assign out_11 = in_8 ? out_13 : 8'bz;  // Controlled_Buffer controlled_buffer_2
endmodule

module alu (
  input  [7:0] in_1,
  input  [7:0] in_2,
  input  in_3,
  input  in_4,
  output [7:0] out_5
);

  wire [7:0] adder_1_out, multiplexer_1_out, subtractor_1_out;

  Adder adder_1 (.a(in_1), .b(in_2), .out(adder_1_out));  // open: cin, cout
  Subtractor subtractor_1 (.a(in_1), .b(in_2), .out(subtractor_1_out));  // open: bin, bout
  assign out_5 = in_4 ? multiplexer_1_out : 8'bz;  // Controlled_Buffer controlled_buffer_1
  Multiplexer #(.width(8)) multiplexer_1 (
    .in0(adder_1_out), .in1(subtractor_1_out), .out(multiplexer_1_out), .sel(in_3));
endmodule
