// Logisim project CompBasedArchUlt.circ as structural Verilog: 4 circuits, main circuit main
module main (
);

  wire clock_1_out;
  wire [1:0] rom_1_data_2, rom_1_data_3, rom_1_data_4;
  wire [2:0] rom_1_data_5, rom_1_data_6;
  wire [3:0] registers_1_out_15, registers_1_out_15_2;
  wire [7:0] counters_1_out_12, counters_1_out_13, counters_1_out_14, counters_1_out_15, registers_1_out_7,
       registers_1_out_8, registers_1_out_9, registers_1_out_10, registers_1_out_11, registers_1_out_12,
       registers_1_out_13, registers_1_out_14;
  wire [29:0] rom_1_data;

  registers registers_1 (
    .in_2(clock_1_out), .in_3(rom_1_data[29]), .in_5(rom_1_data[25]), .in_4(rom_1_data_6),
    .in_6(rom_1_data_5), .in_1(registers_1_out_7), .out_10(registers_1_out_10), .out_11(registers_1_out_11),
    .out_12(registers_1_out_12), .out_13(registers_1_out_13), .out_14(registers_1_out_14),
    .out_15({registers_1_out_15_2, registers_1_out_15}), .out_7(registers_1_out_7),
    .out_8(registers_1_out_8), .out_9(registers_1_out_9));
  alu alu_1 (
    .in_3(rom_1_data_2), .in_4(rom_1_data[11]), .in_1(registers_1_out_8), .in_2(registers_1_out_9),
    .out_5(registers_1_out_7));
  counters counters_1 (
    .in_10(rom_1_data[12]), .in_2(clock_1_out), .in_3(rom_1_data[21]), .in_4(rom_1_data_4),
    .in_5(rom_1_data[18]), .in_6(rom_1_data_3), .in_1(registers_1_out_7), .in_7(rom_1_data[15]),
    .in_8(rom_1_data[14]), .in_9(rom_1_data[13]), .out_15(counters_1_out_15), .out_11(registers_1_out_7),
    .out_12(counters_1_out_12), .out_13(counters_1_out_13), .out_14(counters_1_out_14));
  Clock clock_1 (.out(clock_1_out));
  assign registers_1_out_7 = rom_1_data[8] ? rom_1_data[7:0] : 8'bz;  // Controlled_Buffer controlled_buffer_1
  Hex_Digit_Display hex_digit_display_1 (.value(registers_1_out_15_2));  // open: dp
  Hex_Digit_Display hex_digit_display_2 (.value(registers_1_out_15));  // open: dp
  ROM #(.dataWidth(30)) rom_1 (
    .addr(counters_1_out_15),
    .data({rom_1_data[29], rom_1_data_6, rom_1_data[25], rom_1_data_5, rom_1_data[21], rom_1_data_4, rom_1_data[18], rom_1_data_3, rom_1_data[15:11], rom_1_data_2, rom_1_data[8:0]}));

  // Notes on the sheet:
  //   contents of rom_1 (hex, n*v repeats v):
  //   3c001102
endmodule

module registers (
  input  [7:0] in_1,
  input  in_2,
  input  in_3,
  input  [2:0] in_4,
  input  in_5,
  input  [2:0] in_6,
  output [7:0] out_7,
  output [7:0] out_8,
  output [7:0] out_9,
  output [7:0] out_10,
  output [7:0] out_11,
  output [7:0] out_12,
  output [7:0] out_13,
  output [7:0] out_14,
  output [7:0] out_15
);

  wire decoder_1_out0, decoder_1_out1, decoder_1_out2, decoder_1_out3, decoder_1_out4, decoder_1_out5,
       decoder_1_out6, decoder_1_out7, decoder_2_out0, decoder_2_out1, decoder_2_out2, decoder_2_out3,
       decoder_2_out4, decoder_2_out5, decoder_2_out6, decoder_2_out7;

  Decoder #(.select(3)) decoder_1 (
    .out0(decoder_1_out0), .out1(decoder_1_out1), .out2(decoder_1_out2), .out3(decoder_1_out3),
    .out4(decoder_1_out4), .out5(decoder_1_out5), .out6(decoder_1_out6), .out7(decoder_1_out7), .sel(in_4),
    .en(in_3));
  Decoder #(.select(3)) decoder_2 (
    .out0(decoder_2_out0), .out1(decoder_2_out1), .out2(decoder_2_out2), .out3(decoder_2_out3),
    .out4(decoder_2_out4), .out5(decoder_2_out5), .out6(decoder_2_out6), .out7(decoder_2_out7), .sel(in_6),
    .en(in_5));
  assign out_7 = decoder_2_out0 ? out_8 : 8'bz;  // Controlled_Buffer controlled_buffer_1
  Register register_1 (.D(in_1), .en(decoder_1_out0), .Q(out_8), .clk(in_2));  // open: clr
  Register register_2 (.D(in_1), .en(decoder_1_out1), .Q(out_9), .clk(in_2));  // open: clr
  assign out_7 = decoder_2_out1 ? out_9 : 8'bz;  // Controlled_Buffer controlled_buffer_2
  Register register_3 (.D(in_1), .en(decoder_1_out2), .Q(out_10), .clk(in_2));  // open: clr
  assign out_7 = decoder_2_out2 ? out_10 : 8'bz;  // Controlled_Buffer controlled_buffer_3
  Register register_4 (.D(in_1), .en(decoder_1_out3), .Q(out_11), .clk(in_2));  // open: clr
  assign out_7 = decoder_2_out3 ? out_11 : 8'bz;  // Controlled_Buffer controlled_buffer_4
  Register register_5 (.D(in_1), .en(decoder_1_out4), .Q(out_12), .clk(in_2));  // open: clr
  assign out_7 = decoder_2_out4 ? out_12 : 8'bz;  // Controlled_Buffer controlled_buffer_5
  Register register_6 (.D(in_1), .en(decoder_1_out5), .Q(out_13), .clk(in_2));  // open: clr
  assign out_7 = decoder_2_out5 ? out_13 : 8'bz;  // Controlled_Buffer controlled_buffer_6
  Register register_7 (.D(in_1), .en(decoder_1_out6), .Q(out_14), .clk(in_2));  // open: clr
  assign out_7 = decoder_2_out6 ? out_14 : 8'bz;  // Controlled_Buffer controlled_buffer_7
  assign out_7 = decoder_2_out7 ? out_15 : 8'bz;  // Controlled_Buffer controlled_buffer_8
  Register register_8 (.D(in_1), .en(decoder_1_out7), .Q(out_15), .clk(in_2));  // open: clr
endmodule

module counters (
  input  [7:0] in_1,
  input  in_2,
  input  in_3,
  input  [1:0] in_4,
  input  in_5,
  input  [1:0] in_6,
  input  in_7,
  input  in_8,
  input  in_9,
  input  in_10,
  output [7:0] out_11,
  output [7:0] out_12,
  output [7:0] out_13,
  output [7:0] out_14,
  output [7:0] out_15
);

  wire decoder_1_out0, decoder_1_out1, decoder_1_out2, decoder_1_out3, decoder_2_out0, decoder_2_out1,
       decoder_2_out2, decoder_2_out3;

  Decoder #(.select(2)) decoder_1 (
    .out0(decoder_1_out0), .out1(decoder_1_out1), .out2(decoder_1_out2), .out3(decoder_1_out3), .sel(in_4),
    .en(in_3));
  Decoder #(.select(2)) decoder_2 (
    .out0(decoder_2_out0), .out1(decoder_2_out1), .out2(decoder_2_out2), .out3(decoder_2_out3), .sel(in_6),
    .en(in_5));
  Counter counter_1 (.load(decoder_1_out0), .D(in_1), .count(in_7), .Q(out_12), .clk(in_2));  // open: carry, up, clr
  assign out_11 = decoder_2_out0 ? out_12 : 8'bz;  // Controlled_Buffer controlled_buffer_1
  Counter counter_2 (.load(decoder_1_out1), .D(in_1), .count(in_8), .Q(out_13), .clk(in_2));  // open: carry, up, clr
  assign out_11 = decoder_2_out1 ? out_13 : 8'bz;  // Controlled_Buffer controlled_buffer_2
  assign out_11 = decoder_2_out2 ? out_14 : 8'bz;  // Controlled_Buffer controlled_buffer_3
  Counter counter_3 (.load(decoder_1_out2), .D(in_1), .count(in_9), .Q(out_14), .clk(in_2));  // open: carry, up, clr
  Counter counter_4 (.load(decoder_1_out3), .D(in_1), .count(in_10), .Q(out_15), .clk(in_2));  // open: carry, up, clr
  assign out_11 = decoder_2_out3 ? out_15 : 8'bz;  // Controlled_Buffer controlled_buffer_4
endmodule

module alu (
  input  [7:0] in_1,
  input  [7:0] in_2,
  input  [1:0] in_3,
  input  in_4,
  output [7:0] out_5
);

  wire [7:0] adder_1_out, and_1_out, multiplexer_1_out, or_1_out, subtractor_1_out;

  Adder adder_1 (.a(in_1), .b(in_2), .out(adder_1_out));  // open: cin, cout
  Subtractor subtractor_1 (.a(in_1), .b(in_2), .out(subtractor_1_out));  // open: bin, bout
  assign and_1_out = in_1 & in_2;  // AND_Gate and_1, 8 bits wide
  assign or_1_out = in_1 | in_2;  // OR_Gate or_1, 8 bits wide
  Multiplexer #(.select(2), .width(8)) multiplexer_1 (
    .in0(adder_1_out), .in1(subtractor_1_out), .in2(and_1_out), .in3(or_1_out), .out(multiplexer_1_out),
    .sel(in_3));
  assign out_5 = in_4 ? multiplexer_1_out : 8'bz;  // Controlled_Buffer controlled_buffer_1
endmodule
